// Logisim project LC-3.circ as structural Verilog: 4 circuits, main circuit main
module main (
);

  wire clock, Decode, Evaluate, Execute, Fetch, FetchOps, multiplexer_2_out, multiplexer_4_out, Store;
  wire [2:0] dstReg, OutputR1, OutputR2;
  wire [3:0] Instruction;
  wire [8:0] InstructionReg;
  wire [15:0] adder_1_out, adder_2_out, dstRegVal, JMP, memory, multiplexer_1_out, multiplexer_3_out,
       multiplexer_5_out, Offset6, Offset9, PC, Reg1Val, Reg2Val, Val;

  Adder #(.width(16)) adder_1 (.a(Offset9), .b(PC), .out(adder_1_out));  // open: cin, cout
  Adder #(.width(16)) adder_2 (.a(Offset6), .b(Reg1Val), .out(adder_2_out));  // open: cin, cout
  Multiplexer #(.select(4), .width(16)) multiplexer_1 (
    .in2(adder_1_out), .in3(adder_1_out), .in6(adder_2_out), .in7(adder_2_out), .out(multiplexer_1_out),
    .sel(Instruction));  // open: in0, in1, in4, in5, in8, in9, in10, in11, in12, in13, in14, in15
  Multiplexer #(.select(4)) multiplexer_2 (
    .in0(1'b0), .in1(1'b0), .in2(1'b0), .in3(Execute), .in4(1'b0), .in5(1'b0), .in6(1'b0), .in7(Execute),
    .in8(1'b0), .in9(1'b0), .in10(1'b0), .in11(1'b0), .in12(1'b0), .in13(1'b0), .in14(1'b0), .in15(1'b0),
    .out(multiplexer_2_out), .sel(Instruction));
  Multiplexer #(.width(16)) multiplexer_3 (.in0(PC), .in1(multiplexer_1_out), .out(multiplexer_3_out), .sel(Execute));
  RAM #(.addrWidth(16), .dataWidth(16)) ram_1 (
    .addr(multiplexer_3_out), .we(multiplexer_2_out), .oe(1'b1), .clk(clock), .din(dstRegVal), .dout(memory));
  Multiplexer #(.select(4)) multiplexer_4 (
    .in0(1'b0), .in1(Store), .in2(Store), .in3(1'b0), .in4(1'b0), .in5(Store), .in6(Store), .in7(1'b0),
    .in8(1'b0), .in9(Store), .in10(1'b0), .in11(1'b0), .in12(1'b0), .in13(1'b0), .in14(1'b0), .in15(1'b0),
    .out(multiplexer_4_out), .sel(Instruction));
  Multiplexer #(.select(4), .width(16)) multiplexer_5 (
    .in0(Val), .in1(Val), .in2(memory), .in3(Val), .in4(Val), .in5(Val), .in6(memory), .in7(Val), .in8(Val),
    .in9(Val), .in10(Val), .in11(Val), .in12(Val), .in13(Val), .in14(Val), .in15(Val),
    .out(multiplexer_5_out), .sel(Instruction));
  Clock clock_1 (.out(clock));
  ControlUnit controlunit_1 (
    .Clock1(clock), .InstructionReg(memory), .JUMP(JMP), .Store(Store), .Fetch(Fetch), .Decode(Decode),
    .Evaluate(Evaluate), .FetchOps(FetchOps), .Execute(Execute),
    .Instruction({Instruction, dstReg, InstructionReg}), .ProgramCounter(PC));
  ALU alu_1 (
    .SRCReg1(Reg1Val), .SRCReg2(Reg2Val), .InstructionReg({Instruction, dstReg, InstructionReg}),
    .CalcValue(Val));
  RegFile regfile_1 (
    .SRCReg1(OutputR1), .dst_val(multiplexer_5_out), .enable(multiplexer_4_out), .dst(dstReg),
    .Clock2(clock), .SRCReg2(OutputR2), .Output1(Reg1Val), .Output2(Reg2Val), .Output3(dstRegVal));
  Multiplexer #(.select(4), .width(16)) multiplexer_6 (
    .in12(Reg1Val), .out(JMP), .sel(Instruction));  // open: in0, in1, in2, in3, in4, in5, in6, in7, in8, in9, in10, in11, in13, in14, in15
  assign Offset6 = {{10{InstructionReg[5]}}, InstructionReg[5:0]};  // Bit_Extender bit_extender_1
  assign Offset9 = {{7{InstructionReg[8]}}, InstructionReg};  // Bit_Extender bit_extender_2

  // Other names for the same wires on the sheet: Reg2[2:0] = InstructionReg[2:0]; Reg1[2:0] = InstructionReg[8:6];
  //   InstructionReg[15:9] = {Instruction, dstReg}
endmodule

module ALU (
  input  [15:0] SRCReg1,
  input  [15:0] SRCReg2,
  input  [15:0] InstructionReg,
  output [15:0] CalcValue
);

  wire [15:0] adder_1_out, and_1_out, bit_extender_1_out, multiplexer_1_out, not_1_out;

  assign bit_extender_1_out = {{11{InstructionReg[4]}}, InstructionReg[4:0]};  // Bit_Extender bit_extender_1
  Multiplexer #(.width(16)) multiplexer_1 (
    .in0(SRCReg2), .in1(bit_extender_1_out), .out(multiplexer_1_out), .sel(InstructionReg[5]));
  assign not_1_out = ~SRCReg1;  // NOT_Gate not_1, 16 bits wide
  assign and_1_out = SRCReg1 & multiplexer_1_out;  // AND_Gate and_1, 16 bits wide
  Adder #(.width(16)) adder_1 (.a(SRCReg1), .b(multiplexer_1_out), .out(adder_1_out));  // open: cin, cout
  Multiplexer #(.select(4), .width(16)) multiplexer_2 (
    .in1(adder_1_out), .in5(and_1_out), .in9(not_1_out), .out(CalcValue), .sel(InstructionReg[15:12]));  // open: in0, in2, in3, in4, in6, in7, in8, in10, in11, in12, in13, in14, in15
endmodule

module RegFile (
  input  [2:0] SRCReg1,
  input  [15:0] dst_val,
  input  enable,
  input  [2:0] dst,
  input  Clock2,
  input  [2:0] SRCReg2,
  output [15:0] Output1,
  output [15:0] Output2,
  output [15:0] Output3
);

  wire demultiplexer_1_out0, demultiplexer_1_out1, demultiplexer_1_out2, demultiplexer_1_out3,
       demultiplexer_1_out4, demultiplexer_1_out5, demultiplexer_1_out6, demultiplexer_1_out7;
  wire [15:0] OutputR0, OutputR1, OutputR2, OutputR3, OutputR4, OutputR5, OutputR6, OutputR7;

  Demultiplexer #(.enable("true"), .select(3)) demultiplexer_1 (
    .out0(demultiplexer_1_out0), .out1(demultiplexer_1_out1), .out2(demultiplexer_1_out2),
    .out3(demultiplexer_1_out3), .out4(demultiplexer_1_out4), .out5(demultiplexer_1_out5),
    .out6(demultiplexer_1_out6), .out7(demultiplexer_1_out7), .in(enable), .sel(dst));  // open: en
  Register #(.width(16)) R0 (.D(dst_val), .en(demultiplexer_1_out0), .clk(Clock2), .Q(OutputR0));  // open: clr
  Register #(.width(16)) R2 (.D(dst_val), .en(demultiplexer_1_out2), .clk(Clock2), .Q(OutputR2));  // open: clr
  Register #(.width(16)) R4 (.D(dst_val), .en(demultiplexer_1_out4), .clk(Clock2), .Q(OutputR4));  // open: clr
  Register #(.width(16)) R6 (.D(dst_val), .en(demultiplexer_1_out6), .clk(Clock2), .Q(OutputR6));  // open: clr
  Register #(.width(16)) R1 (.D(dst_val), .en(demultiplexer_1_out1), .clk(Clock2), .Q(OutputR1));  // open: clr
  Register #(.width(16)) R3 (.D(dst_val), .en(demultiplexer_1_out3), .clk(Clock2), .Q(OutputR3));  // open: clr
  Register #(.width(16)) R5 (.D(dst_val), .en(demultiplexer_1_out5), .clk(Clock2), .Q(OutputR5));  // open: clr
  Register #(.width(16)) R7 (.D(dst_val), .en(demultiplexer_1_out7), .clk(Clock2), .Q(OutputR7));  // open: clr
  Multiplexer #(.select(3), .width(16)) multiplexer_1 (
    .in0(OutputR0), .in1(OutputR1), .in2(OutputR2), .in3(OutputR3), .in4(OutputR4), .in5(OutputR5),
    .in6(OutputR6), .in7(OutputR7), .out(Output1), .sel(SRCReg1));
  Multiplexer #(.select(3), .width(16)) multiplexer_2 (
    .in0(OutputR0), .in1(OutputR1), .in2(OutputR2), .in3(OutputR3), .in4(OutputR4), .in5(OutputR5),
    .in6(OutputR6), .in7(OutputR7), .out(Output2), .sel(SRCReg2));
  Multiplexer #(.select(3), .width(16)) multiplexer_3 (
    .in0(OutputR0), .in1(OutputR1), .in2(OutputR2), .in3(OutputR3), .in4(OutputR4), .in5(OutputR5),
    .in6(OutputR6), .in7(OutputR7), .out(Output3), .sel(dst));

  // Other names for the same wires on the sheet: c = Clock2; Val[15:0] = dst_val
endmodule

module ControlUnit (
  input  Clock1,
  input  [15:0] InstructionReg,
  input  [15:0] JUMP,
  output Store,
  output Fetch,
  output Decode,
  output Evaluate,
  output FetchOps,
  output Execute,
  output [15:0] Instruction,
  output [15:0] ProgramCounter
);

  wire [2:0] counter_1_q;
  wire [15:0] adder_1_out, multiplexer_1_out;

  Adder #(.width(16)) adder_1 (.a(ProgramCounter), .b(16'h1), .out(adder_1_out));  // open: cin, cout
  Counter #(.max('h5), .width(3)) counter_1 (.clk(Clock1), .Q(counter_1_q));  // open: clr, load, up, count, D, carry
  Multiplexer #(.select(4), .width(16)) multiplexer_1 (
    .in0(adder_1_out), .in1(adder_1_out), .in2(adder_1_out), .in3(adder_1_out), .in4(adder_1_out),
    .in5(adder_1_out), .in6(adder_1_out), .in7(adder_1_out), .in8(adder_1_out), .in9(adder_1_out),
    .in10(adder_1_out), .in11(adder_1_out), .in12(JUMP), .in13(adder_1_out), .in14(adder_1_out),
    .in15(adder_1_out), .out(multiplexer_1_out), .sel(Instruction[15:12]));
  Register #(.width(16)) PC (.D(multiplexer_1_out), .en(Decode), .clk(Clock1), .Q(ProgramCounter));  // open: clr
  Demultiplexer #(.select(3)) demultiplexer_1 (
    .out0(Store), .out1(Fetch), .out2(Decode), .out3(Evaluate), .out4(FetchOps), .out5(Execute), .in(1'b1),
    .sel(counter_1_q));  // open: out6, out7
  Register #(.width(16)) IR (.D(InstructionReg), .en(Fetch), .clk(Clock1), .Q(Instruction));  // open: clr

  // Other names for the same wires on the sheet: FetchVal = Fetch; Instruction_t[3:0] = Instruction[15:12]
endmodule
